# Fritzing sketch Circuit Schematic (saved by Fritzing 0.9.3b)
breadboards: 1

parts:
  Part5 = Bluetooth HC-05 Macho
  MIC1 = Microphone
  Part1 = Arduino Uno (Rev3)
  MIC2 = Microphone
  MIC3 = Microphone
  Part6 = Arduino Motor Shield (Rev3)
  M1 = DC Motor
  M2 = DC Motor
  VCC1 = 4 x AAA Battery Mount
  VCC2 = 4 x AAA Battery Mount
  Raspberry_Pi_1 = Raspberry Pi 3 [part_number=RPI-3-V1.2]  # not connected

nets:
  N1: Part5.State, Part1.D2
  N2: Part5.TXD, Part1.D0/RX
  N3: Part5.RXD, Part1.D1/TX
  5V: Part5.VCC, Part1.5V, Part6.5V, M1.pin_1, M2.pin_1
  GND: Part5.GND, MIC1.pin1, Part1.GND, MIC2.pin1, MIC3.pin1, Part6.GND, M1.pin_2, M2.pin_2, VCC2.-
  N4: MIC1.pin2, Part1.A3
  N5: Part1.A1, MIC2.pin2
  N6: Part1.A2, MIC3.pin2
  N7: Part1.D9_PWM, Part6.D9/BreakeA
  N8: Part1.D10_PWM/SS, Part6.D10_PWM
  N9: Part1.D5_PWM, Part6.D5_PWM
  N10: Part1.D6_PWM, Part6.D6_PWM
  N11: Part6.VMOT, VCC1.+
